# Fritzing sketch BaseSchematic (saved by Fritzing 0.7.12b)
breadboards: 1

parts:
  Arduino1 = Arduino
  Striscia_LED_RGB = RGB LED (com. anode, rbg) [package="5 mm [THT]"]
  R_MOS = Basic FET N-Channel [part_number=IRF520 package="D2Pak [SMD]"]
  G_MOS = Basic FET N-Channel [part_number=IRF520 package="D2Pak [SMD]"]
  B_MOS = Basic FET N-Channel [part_number=IRF520 package="D2Pak [SMD]"]
  LED1 = LED - 3mm [color="Red (633nm)" part_number="Red 3mm" package="3 mm [THT]"]
  LED2 = LED - 3mm [color="Red (633nm)" part_number="Red 3mm" package="3 mm [THT]"]
  LED3 = LED - 3mm [color="Red (633nm)" part_number="Red 3mm" package="3 mm [THT]"]
  LED4 = LED - 3mm [color="Red (633nm)" part_number="Red 3mm" package="3 mm [THT]"]
  LED5 = LED - 3mm [color="Red (633nm)" part_number="Red 3mm" package="3 mm [THT]"]
  LED6 = LED - 3mm [color="Red (633nm)" part_number="Red 3mm" package="3 mm [THT]"]
  R1 = Resistor [tolerance=±5% resistance=330 part_number=330Ω package=THT]
  CO2_Sensor = IC, DIP package, 4 pins [chip_label="T 6613"]

nets:
  GND: Arduino1.GND, R_MOS.source, G_MOS.source, B_MOS.source, R1.Pin_1, CO2_Sensor.pin2
  N1: Arduino1.D9, LED1.anode
  N2: Arduino1.D8, LED2.anode
  N3: Arduino1.D7, LED3.anode
  N4: Arduino1.D6, R_MOS.Gate
  N5: Arduino1.D5, G_MOS.Gate
  N6: Arduino1.D3, B_MOS.Gate
  N7: Arduino1.D2, LED4.anode
  N8: Arduino1.D1TX, LED5.anode
  N9: Arduino1.D0RX, LED6.anode
  N10: Arduino1.+5V, CO2_Sensor.pin1
  N11: Arduino1.A0, CO2_Sensor.pin3
  N12: Striscia_LED_RGB.red_cathode, R_MOS.drain
  12V: Striscia_LED_RGB.common_anode
  N13: Striscia_LED_RGB.blue_cathode, B_MOS.drain
  N14: Striscia_LED_RGB.green_cathode, G_MOS.drain
  N15: LED1.cathode, LED2.cathode, LED3.cathode, LED4.cathode, LED5.cathode, LED6.cathode, R1.Pin_0
